// Logisim project 2-bit Multiplier.circ as structural Verilog: 1 circuit, main circuit main
module main (
  input  A0,
  input  B0,
  input  A1,
  input  B1
);

  wire and_1_out, and_2_out, and_3_out, and_4_out, and_5_out, not_1_out, not_2_out, or_1_out, xor_1_out;

  and and_1 (and_1_out, A0, B0);
  and and_2 (and_2_out, A0, A1);
  and and_3 (and_3_out, B0, B1);
  not not_1 (not_1_out, B0);
  not not_2 (not_2_out, A0);
  or or_1 (or_1_out, not_1_out, not_2_out);
  and and_4 (and_4_out, A0, B0, B1, A1);
  xor xor_1 (xor_1_out, and_2_out, and_3_out);
  LED led_1 (.in(and_1_out));
  LED led_2 (.in(xor_1_out));
  and and_5 (and_5_out, A1, B1, or_1_out);
  LED led_3 (.in(and_5_out));
  LED led_4 (.in(and_4_out));

  // Notes on the sheet:
  //   P0
  //   P1
  //   P2
  //   P3
endmodule
