// Logisim project 25DIT027.circ as structural Verilog: 1 circuit, main circuit main
module main (
  input  in_1
);

  wire and_1_out, and_2_out, clock_1_out, j_k_ff_1_q, j_k_ff_2_q, not_1_out, not_2_out, or_1_out, or_2_out;

  Clock clock_1 (.out(clock_1_out));
  J_K_Flip_Flop j_k_ff_1 (.clk(clock_1_out), .Q(j_k_ff_1_q));  // open: J, K, Qn, preset, en, reset
  J_K_Flip_Flop j_k_ff_2 (.clk(clock_1_out), .Q(j_k_ff_2_q));  // open: J, K, Qn, preset, en, reset
  J_K_Flip_Flop j_k_ff_3 (.J(1'b1), .clk(clock_1_out), .K(1'b1));  // open: Q, Qn, preset, en, reset
  not not_1 (not_1_out, j_k_ff_1_q);
  not not_2 (not_2_out, in_1);
  or or_1 (or_1_out, j_k_ff_1_q, j_k_ff_2_q);
  and and_1 (and_1_out, in_1, not_1_out);
  and and_2 (and_2_out, or_1_out, not_2_out);
  or or_2 (or_2_out, and_2_out, and_1_out);
endmodule
