// Logisim project DE Project NEw.circ as structural Verilog: 1 circuit, main circuit main
module main (
  input  in_1
);

  wire and_1_out, and_2_out, and_3_out, and_4_out, and_5_out, and_6_out, clock_1_out, not_1_out, not_2_out,
       not_3_out, or_1_out, or_2_out, t_ff_1_q, t_ff_1_qn, t_ff_2_q, xor_1_out;

  not not_1 (not_1_out, in_1);
  and and_1 (and_1_out, t_ff_1_q, not_1_out);
  and and_2 (and_2_out, in_1, t_ff_2_q);
  xor xor_1 (xor_1_out, in_1, t_ff_2_q);
  and and_3 (and_3_out, t_ff_1_qn, t_ff_2_q);
  or or_1 (or_1_out, and_1_out, and_2_out);
  or or_2 (or_2_out, xor_1_out, and_3_out);
  Clock clock_1 (.out(clock_1_out));
  T_Flip_Flop t_ff_1 (.clk(clock_1_out), .T(or_1_out), .Q(t_ff_1_q), .Qn(t_ff_1_qn));  // open: preset, reset, en
  T_Flip_Flop t_ff_2 (.clk(clock_1_out), .T(or_2_out), .Q(t_ff_2_q));  // open: Qn, preset, reset, en
  LED led_1 (.in(and_4_out));
  and and_4 (and_4_out, not_2_out, t_ff_2_q);
  not not_2 (not_2_out, t_ff_1_q);
  LED led_2 (.in(and_5_out));
  and and_5 (and_5_out, t_ff_1_q, not_3_out);
  not not_3 (not_3_out, t_ff_2_q);
  LED led_3 (.in(and_6_out));
  and and_6 (and_6_out, t_ff_1_q, t_ff_2_q);
endmodule
