// Logisim project Full Adder.circ as structural Verilog: 1 circuit, main circuit main
module main (
  input  A,
  input  B,
  input  C
);

  wire and_1_out, and_2_out, and_3_out, or_1_out, xor_1_out;

  xor xor_1 (xor_1_out, A, B, C);
  and and_1 (and_1_out, C, B);
  and and_2 (and_2_out, C, A);
  and and_3 (and_3_out, A, B);
  or or_1 (or_1_out, and_1_out, and_2_out, and_3_out);
  LED led_1 (.in(xor_1_out));
  LED led_2 (.in(or_1_out));

  // Notes on the sheet:
  //   SUM
  //   CARRY
endmodule
