// Logisim project Full Subtractor.circ as structural Verilog: 1 circuit, main circuit main
module main (
  input  A,
  input  B,
  input  C
);

  wire and_1_out, and_2_out, and_3_out, not_1_out, or_1_out, xor_1_out;

  not not_1 (not_1_out, A);
  xor xor_1 (xor_1_out, A, B, C);
  and and_1 (and_1_out, C, B);
  and and_2 (and_2_out, not_1_out, C);
  and and_3 (and_3_out, not_1_out, B);
  LED led_1 (.in(xor_1_out));
  LED led_2 (.in(or_1_out));
  or or_1 (or_1_out, and_1_out, and_2_out, and_3_out);

  // Notes on the sheet:
  //   DIFFERENCE
  //   BORROW
endmodule
