// Logisim project Internal Practical Exam.circ as structural Verilog: 1 circuit, main circuit main
module main (
);

  wire A_q, A_qn, and_1_out, and_2_out, and_3_out, and_4_out, and_5_out, and_6_out, and_7_out, B_q, B_qn,
       C_q, C_qn, clock_1_out, D_q, D_qn, or_1_out, or_2_out;

  and and_1 (and_1_out, A_qn, B_qn);
  and and_2 (and_2_out, A_q, C_q);
  and and_3 (and_3_out, C_qn, D_q);
  and and_4 (and_4_out, A_q, C_q);
  or or_1 (or_1_out, and_1_out, and_2_out);
  or or_2 (or_2_out, and_3_out, and_4_out);
  and and_5 (and_5_out, D_qn, C_q, B_q);
  and and_6 (and_6_out, A_q, B_q);
  and and_7 (and_7_out, B_q, C_q);
  Clock clock_1 (.out(clock_1_out));
  S_R_Flip_Flop A (.S(and_5_out), .clk(clock_1_out), .R(and_6_out), .Q(A_q), .Qn(A_qn));  // open: preset, reset, en
  S_R_Flip_Flop B (.S(or_1_out), .clk(clock_1_out), .R(and_7_out), .Q(B_q), .Qn(B_qn));  // open: preset, reset, en
  S_R_Flip_Flop C (.S(C_qn), .clk(clock_1_out), .R(or_2_out), .Q(C_q), .Qn(C_qn));  // open: preset, reset, en
  S_R_Flip_Flop D (.S(A_q), .clk(clock_1_out), .R(A_qn), .Q(D_q), .Qn(D_qn));  // open: preset, reset, en
  LED led_1 (.in(A_q));
  LED led_2 (.in(C_q));
  LED led_3 (.in(B_q));
  LED led_4 (.in(D_q));
endmodule
