// Logisim project Practical No. 3.circ as structural Verilog: 1 circuit, main circuit main
module main (
  input  [3:0] in_1,
  input  [3:0] in_2,
  input  [3:0] in_3,
  input  [3:0] in_4,
  output out_5,
  output out_6,
  output out_7
);

  wire comparator_2_eq, comparator_2_gt, comparator_3_eq, comparator_3_gt;
  wire [3:0] adder_1_out, subtractor_1_out;

  Adder #(.width(4)) adder_1 (.a(in_2), .b(in_3), .out(adder_1_out));  // open: cin, cout
  Subtractor #(.width(4)) subtractor_1 (.a(in_2), .b(in_4), .out(subtractor_1_out));  // open: bin, bout
  Comparator #(.width(4)) comparator_1 (.a(in_1), .b(in_2), .gt(out_5));  // open: eq, lt
  Comparator #(.width(4)) comparator_2 (
    .a(in_1), .b(adder_1_out), .gt(comparator_2_gt), .eq(comparator_2_eq));  // open: lt
  Comparator #(.width(4)) comparator_3 (
    .a(in_1), .b(subtractor_1_out), .gt(comparator_3_gt), .eq(comparator_3_eq));  // open: lt
  or or_1 (out_6, comparator_2_gt, comparator_2_eq);
  or or_2 (out_7, comparator_3_gt, comparator_3_eq);
endmodule
