// Logisim project Practical No. 4.circ as structural Verilog: 1 circuit, main circuit main
module main (
  input  [3:0] in_1,
  input  [3:0] in_2,
  input  in_3,
  input  [3:0] in_4,
  input  in_5,
  output [3:0] out_6,
  output [3:0] out_7
);

  wire [3:0] demultiplexer_1_out0, demultiplexer_1_out1, multiplexer_1_out, xor_1_out;

  Multiplexer #(.width(4), .enable("false")) multiplexer_1 (
    .in0(in_1), .in1(in_2), .out(multiplexer_1_out), .sel(in_3));
  assign xor_1_out = multiplexer_1_out ^ in_4;  // XOR_Gate xor_1, 4 bits wide
  Demultiplexer #(.width(4), .enable("false")) demultiplexer_1 (
    .out0(demultiplexer_1_out0), .out1(demultiplexer_1_out1), .in(xor_1_out), .sel(in_5));
  assign out_6 = in_4 ^ demultiplexer_1_out0;  // XOR_Gate xor_2, 4 bits wide
  assign out_7 = demultiplexer_1_out1 ^ in_4;  // XOR_Gate xor_3, 4 bits wide

  // Notes on the sheet:
  //   2:1 Multiplexer to 1:2 Demultiplexer
endmodule
