// Logisim project Practical No. 5.circ as structural Verilog: 1 circuit, main circuit main
module main (
  input  X,
  input  in_2
);

  wire A_q, and_1_out, and_2_out, and_3_out, and_4_out, B_q, B_qn, clock_1_out, j_k_ff_1_q, j_k_ff_1_qn,
       not_1_out, or_1_out, or_2_out;

  not not_1 (not_1_out, X);
  and and_1 (and_1_out, not_1_out, j_k_ff_1_q, B_q);
  and and_2 (and_2_out, X, B_qn, j_k_ff_1_qn);
  and and_3 (and_3_out, j_k_ff_1_qn, X);
  and and_4 (and_4_out, j_k_ff_1_q, not_1_out);
  or or_1 (or_1_out, and_1_out, and_2_out);
  or or_2 (or_2_out, and_3_out, and_4_out);
  Clock clock_1 (.out(clock_1_out));
  J_K_Flip_Flop #(.trigger("falling")) A (
    .J(or_1_out), .clk(clock_1_out), .K(or_1_out), .Q(A_q));  // open: Qn, preset, en, reset
  J_K_Flip_Flop B (.J(or_2_out), .clk(clock_1_out), .K(or_2_out), .Q(B_q), .Qn(B_qn));  // open: preset, en, reset
  J_K_Flip_Flop j_k_ff_1 (
    .J(in_2), .clk(clock_1_out), .K(in_2), .Q(j_k_ff_1_q), .Qn(j_k_ff_1_qn));  // open: preset, en, reset
  LED led_1 (.in(B_q));
  LED led_2 (.in(A_q));
  LED led_3 (.in(j_k_ff_1_q));

  // Notes on the sheet:
  //   BCX'
  //   B'C'X
endmodule
