// Logisim project Practical No. 6.circ as structural Verilog: 1 circuit, main circuit main
module main (
  input  in_1
);

  wire and_1_out, and_2_out, and_3_out, and_4_out, clock_1_out, or_1_out, t_ff_1_q, t_ff_1_qn, t_ff_2_q,
       t_ff_3_q, t_ff_4_q;

  and and_1 (and_1_out, t_ff_1_q, t_ff_4_q);
  and and_2 (and_2_out, t_ff_3_q, t_ff_2_q, t_ff_4_q);
  and and_3 (and_3_out, t_ff_3_q, t_ff_4_q);
  or or_1 (or_1_out, and_1_out, and_2_out);
  and and_4 (and_4_out, t_ff_1_qn, t_ff_4_q);
  Clock clock_1 (.out(clock_1_out));
  T_Flip_Flop t_ff_1 (.clk(clock_1_out), .T(or_1_out), .Q(t_ff_1_q), .Qn(t_ff_1_qn));  // open: preset, reset, en
  T_Flip_Flop t_ff_2 (.clk(clock_1_out), .T(and_3_out), .Q(t_ff_2_q));  // open: Qn, preset, reset, en
  T_Flip_Flop t_ff_3 (.clk(clock_1_out), .T(and_4_out), .Q(t_ff_3_q));  // open: Qn, preset, reset, en
  T_Flip_Flop t_ff_4 (.clk(clock_1_out), .T(in_1), .Q(t_ff_4_q));  // open: Qn, preset, reset, en
  LED led_1 (.in(t_ff_1_q));
  LED led_2 (.in(t_ff_2_q));
  LED led_3 (.in(t_ff_3_q));
  LED led_4 (.in(t_ff_4_q));

  // Notes on the sheet:
  //   A
  //   D
  //   C
  //   B
  //   C
  //   D
  //   AD
  //   BCD
  //   A'
  //   D
  //   A
  //   A'
  //   B
  //   C
  //   D
endmodule
