// Logisim project Practical No. 7.circ as structural Verilog: 1 circuit, main circuit main
module main (
);

  wire and_1_out, and_2_out, and_3_out, and_4_out, clock_1_out, d_ff_1_q, d_ff_1_qn, d_ff_2_q, d_ff_2_qn,
       d_ff_3_q, d_ff_3_qn, d_ff_4_q, d_ff_4_qn, or_1_out, or_2_out, xor_1_out;

  and and_1 (and_1_out, d_ff_3_qn, d_ff_4_q);
  and and_2 (and_2_out, d_ff_4_q, d_ff_2_qn, d_ff_1_qn);
  and and_3 (and_3_out, d_ff_3_q, d_ff_4_qn);
  and and_4 (and_4_out, d_ff_3_q, d_ff_2_q);
  xor xor_1 (xor_1_out, d_ff_4_q, d_ff_3_q);
  or or_1 (or_1_out, and_1_out, and_2_out);
  or or_2 (or_2_out, d_ff_1_q, d_ff_2_q, and_3_out);
  Clock clock_1 (.out(clock_1_out));
  D_Flip_Flop d_ff_1 (.clk(clock_1_out), .D(and_4_out), .Q(d_ff_1_q), .Qn(d_ff_1_qn));  // open: preset, en, reset
  D_Flip_Flop d_ff_2 (.clk(clock_1_out), .D(xor_1_out), .Q(d_ff_2_q), .Qn(d_ff_2_qn));  // open: preset, en, reset
  D_Flip_Flop d_ff_3 (.clk(clock_1_out), .D(or_1_out), .Q(d_ff_3_q), .Qn(d_ff_3_qn));  // open: preset, en, reset
  D_Flip_Flop d_ff_4 (.clk(clock_1_out), .D(or_2_out), .Q(d_ff_4_q), .Qn(d_ff_4_qn));  // open: preset, en, reset
  LED led_1 (.in(d_ff_1_q));
  LED led_2 (.in(d_ff_2_q));
  LED led_3 (.in(d_ff_4_q));
  LED led_4 (.in(d_ff_3_q));
endmodule
